// Logisim project PHANTOM_32.circ as structural Verilog
module alu (
  input  [3:0] op,
  input  [31:0] lhs,
  input  [31:0] rhs,
  output [31:0] result
);

  wire [0:0] comparator_1_lt, comparator_2_lt;
  wire [31:0] adder_1_out, and_1_out, nor_1_out, or_1_out, shifter_1_out, shifter_2_out, shifter_3_out,
       subtractor_1_out;

  Adder #(.width(32)) adder_1 (.a(lhs), .b(rhs), .out(adder_1_out), .cin(1'b0));  // open: cout
  Subtractor #(.width(32)) subtractor_1 (.a(lhs), .b(rhs), .out(subtractor_1_out), .bin(1'b0));  // open: bout
  assign and_1_out = lhs & rhs;  // AND_Gate and_1, 32 bits wide
  assign or_1_out = lhs | rhs;  // OR_Gate or_1, 32 bits wide
  assign nor_1_out = ~(lhs | rhs);  // NOR_Gate nor_1, 32 bits wide
  Shifter #(.width(32)) shifter_1 (.in(lhs), .\dist (rhs[4:0]), .out(shifter_1_out));
  Shifter #(.shift("lr"), .width(32)) shifter_2 (.in(lhs), .\dist (rhs[4:0]), .out(shifter_2_out));
  Shifter #(.shift("ar"), .width(32)) shifter_3 (.in(lhs), .\dist (rhs[4:0]), .out(shifter_3_out));
  Comparator #(.width(32)) comparator_1 (.a(lhs), .b(rhs), .lt(comparator_1_lt[0]));  // open: gt, eq
  Comparator #(.mode("unsigned"), .width(32)) comparator_2 (.a(lhs), .b(rhs), .lt(comparator_2_lt[0]));  // open: gt, eq
  Multiplexer #(.select(4), .width(32)) multiplexer_1 (
    .in0(adder_1_out), .in1(subtractor_1_out), .in2(and_1_out), .in3(or_1_out), .in4(nor_1_out),
    .in5(shifter_1_out), .in6(shifter_2_out), .in7(shifter_3_out), .in8({{31{1'b0}}, comparator_1_lt[0]}),
    .in9({{31{1'b0}}, comparator_2_lt[0]}), .in10(rhs), .in11(32'hdeadbeef), .in12(32'hdeadbeef),
    .in13(32'hdeadbeef), .in14(32'hdeadbeef), .in15(32'hdeadbeef), .out(result));  // open: sel
endmodule

module regfile (
  input  [4:0] rd_index_a,
  input  [4:0] wr_index,
  input  [31:0] wr_data,
  input  wr_en,
  input  clk,
  input  [4:0] rd_index_b,
  output [31:0] rd_data_a,
  output [31:0] rd_data_b
);

  wire and_1_out, and_2_out, and_3_out, and_4_out, and_5_out, and_6_out, and_7_out, and_8_out;
  wire [31:0] decoder_1_out0, register_1_q, register_2_q, register_3_q, register_4_q, register_5_q,
       register_6_q, register_7_q, register_8_q, register_9_q, register_10_q, register_11_q, register_12_q,
       register_13_q, register_14_q, register_15_q, register_16_q, register_17_q, register_18_q,
       register_19_q, register_20_q, register_21_q, register_22_q, register_23_q, register_24_q,
       register_25_q, register_26_q, register_27_q, register_28_q, register_29_q, register_30_q,
       register_31_q, register_32_q, undriven, undriven_2, undriven_3;

  Decoder #(.enable("false"), .select(5)) decoder_1 (
    .out0(decoder_1_out0[0]), .out1(decoder_1_out0[1]), .out2(decoder_1_out0[2]), .out3(decoder_1_out0[3]),
    .out4(decoder_1_out0[4]), .out5(decoder_1_out0[5]), .out6(decoder_1_out0[6]), .out7(decoder_1_out0[7]),
    .out8(decoder_1_out0[8]), .out9(decoder_1_out0[9]), .out10(decoder_1_out0[10]),
    .out11(decoder_1_out0[11]), .out12(decoder_1_out0[12]), .out13(decoder_1_out0[13]),
    .out14(decoder_1_out0[14]), .out15(decoder_1_out0[15]), .out16(decoder_1_out0[16]),
    .out17(decoder_1_out0[17]), .out18(decoder_1_out0[18]), .out19(decoder_1_out0[19]),
    .out20(decoder_1_out0[20]), .out21(decoder_1_out0[21]), .out22(decoder_1_out0[22]),
    .out23(decoder_1_out0[23]), .out24(decoder_1_out0[24]), .out25(decoder_1_out0[25]),
    .out26(decoder_1_out0[26]), .out27(decoder_1_out0[27]), .out28(decoder_1_out0[28]),
    .out29(decoder_1_out0[29]), .out30(decoder_1_out0[30]), .out31(decoder_1_out0[31]), .sel(wr_index));
  Register #(.width(32)) register_1 (.D(wr_data), .en(and_1_out), .clk(clk), .Q(register_1_q), .clr(1'b0));
  and and_1 (and_1_out, decoder_1_out0[0], wr_en);
  Register #(.width(32)) register_2 (.D(wr_data), .en(and_2_out), .clk(clk), .Q(register_2_q), .clr(1'b0));
  and and_2 (and_2_out, decoder_1_out0[1], wr_en);
  Register #(.width(32)) register_3 (.D(wr_data), .en(and_3_out), .clk(clk), .Q(register_3_q), .clr(1'b0));
  and and_3 (and_3_out, decoder_1_out0[2], wr_en);
  Register #(.width(32)) register_4 (.D(wr_data), .en(and_4_out), .clk(clk), .Q(register_4_q), .clr(1'b0));
  and and_4 (and_4_out, decoder_1_out0[3], wr_en);
  Register #(.width(32)) register_5 (.D(wr_data), .en(and_5_out), .clk(clk), .Q(register_5_q), .clr(1'b0));
  and and_5 (and_5_out, decoder_1_out0[4], wr_en);
  Register #(.width(32)) register_6 (.D(wr_data), .en(and_6_out), .clk(clk), .Q(register_6_q), .clr(1'b0));
  and and_6 (and_6_out, decoder_1_out0[5], wr_en);
  Register #(.width(32)) register_7 (.D(wr_data), .en(and_7_out), .clk(clk), .Q(register_7_q), .clr(1'b0));
  and and_7 (and_7_out, decoder_1_out0[6], wr_en);
  Register #(.width(32)) register_8 (.D(wr_data), .en(and_8_out), .clk(clk), .Q(register_8_q), .clr(1'b0));
  and and_8 (and_8_out, decoder_1_out0[7], wr_en);
  Register #(.width(32)) register_9 (.D(undriven), .en(wr_en), .clk(clk), .Q(register_9_q), .clr(1'b0));
  Register #(.width(32)) register_10 (.D(undriven), .en(wr_en), .clk(clk), .Q(register_10_q), .clr(1'b0));
  Register #(.width(32)) register_11 (.D(undriven), .en(wr_en), .clk(clk), .Q(register_11_q), .clr(1'b0));
  Register #(.width(32)) register_12 (.D(undriven), .en(wr_en), .clk(clk), .Q(register_12_q), .clr(1'b0));
  Register #(.width(32)) register_13 (.D(undriven), .en(wr_en), .clk(clk), .Q(register_13_q), .clr(1'b0));
  Register #(.width(32)) register_14 (.D(undriven), .en(wr_en), .clk(clk), .Q(register_14_q), .clr(1'b0));
  Register #(.width(32)) register_15 (.D(undriven), .en(wr_en), .clk(clk), .Q(register_15_q), .clr(1'b0));
  Register #(.width(32)) register_16 (.D(undriven), .en(wr_en), .clk(clk), .Q(register_16_q), .clr(1'b0));
  Register #(.width(32)) register_17 (.D(undriven_2), .en(wr_en), .clk(clk), .Q(register_17_q), .clr(1'b0));
  Register #(.width(32)) register_18 (.D(undriven_2), .en(wr_en), .clk(clk), .Q(register_18_q), .clr(1'b0));
  Register #(.width(32)) register_19 (.D(undriven_2), .en(wr_en), .clk(clk), .Q(register_19_q), .clr(1'b0));
  Register #(.width(32)) register_20 (.D(undriven_2), .en(wr_en), .clk(clk), .Q(register_20_q), .clr(1'b0));
  Register #(.width(32)) register_21 (.D(undriven_2), .en(wr_en), .clk(clk), .Q(register_21_q), .clr(1'b0));
  Register #(.width(32)) register_22 (.D(undriven_2), .en(wr_en), .clk(clk), .Q(register_22_q), .clr(1'b0));
  Register #(.width(32)) register_23 (.D(undriven_2), .en(wr_en), .clk(clk), .Q(register_23_q), .clr(1'b0));
  Register #(.width(32)) register_24 (.D(undriven_2), .en(wr_en), .clk(clk), .Q(register_24_q), .clr(1'b0));
  Register #(.width(32)) register_25 (.D(undriven_3), .en(wr_en), .clk(clk), .Q(register_25_q), .clr(1'b0));
  Register #(.width(32)) register_26 (.D(undriven_3), .en(wr_en), .clk(clk), .Q(register_26_q), .clr(1'b0));
  Register #(.width(32)) register_27 (.D(undriven_3), .en(wr_en), .clk(clk), .Q(register_27_q), .clr(1'b0));
  Register #(.width(32)) register_28 (.D(undriven_3), .en(wr_en), .clk(clk), .Q(register_28_q), .clr(1'b0));
  Register #(.width(32)) register_29 (.D(undriven_3), .en(wr_en), .clk(clk), .Q(register_29_q), .clr(1'b0));
  Register #(.width(32)) register_30 (.D(undriven_3), .en(wr_en), .clk(clk), .Q(register_30_q), .clr(1'b0));
  Register #(.width(32)) register_31 (.D(undriven_3), .en(wr_en), .clk(clk), .Q(register_31_q), .clr(1'b0));
  Register #(.width(32)) register_32 (.D(undriven_3), .en(wr_en), .clk(clk), .Q(register_32_q), .clr(1'b0));
  Multiplexer #(.select(5), .width(32)) multiplexer_1 (
    .in0(register_1_q), .in1(register_2_q), .in2(register_3_q), .in3(register_4_q), .in4(register_5_q),
    .in5(register_6_q), .in6(register_7_q), .in7(register_8_q), .in8(register_9_q), .in9(register_10_q),
    .in10(register_11_q), .in11(register_12_q), .in12(register_13_q), .in13(register_14_q),
    .in14(register_15_q), .in15(register_16_q), .in16(register_17_q), .in17(register_18_q),
    .in18(register_19_q), .in19(register_20_q), .in20(register_21_q), .in21(register_22_q),
    .in22(register_23_q), .in23(register_24_q), .in24(register_25_q), .in25(register_26_q),
    .in26(register_27_q), .in27(register_28_q), .in28(register_29_q), .in29(register_30_q),
    .in30(register_31_q), .in31(register_32_q), .out(rd_data_a), .sel(rd_index_a));
endmodule
